# Fritzing sketch finalProjectSchematic (saved by Fritzing 0.9.10b)
breadboards: 1

parts:
  J1 = Basic Servo
  M1 = Stepper Motor - Bipolar
  Pololu_A1 = Pololu A4988 [package=SO16]
  Part2 = Arduino Mega 2560 (Rev3)
  R2 = PHOTOCELL [package=photocell]
  R3 = PHOTOCELL [package=photocell]
  R4 = PHOTOCELL [package=photocell]
  R1 = PHOTOCELL [package=photocell]
  R5 = Resistor [tolerance=±5% resistance=10 package="0805 [SMD]"]
  R6 = Resistor [tolerance=±5% resistance=10 package="0805 [SMD]"]
  R7 = Resistor [tolerance=±5% resistance=10 package="0805 [SMD]"]
  R8 = Resistor [tolerance=±5% resistance=10 package="0805 [SMD]"]
  J2 = Infrared Proximity Sensor [distance_to_obstacle=50%]
  C1 = Capacitor Polarized [package=cpol-radial-100uf-25v]

nets:
  GND: J1.gnd, Pololu_A1.GND, Part2.GND, R5.Pin_0, R6.Pin_0, R7.Pin_0, R8.Pin_0, J2.GND, C1.-
  VCC: J1.vcc, Part2.IOREF, J2.Vcc
  N1: J1.pulse, Part2.D4_PWM
  N2: M1.A, Pololu_A1.2B
  N3: M1.C, Pololu_A1.2A
  N4: M1.B, Pololu_A1.1A
  N5: M1.D, Pololu_A1.1B
  N6: Pololu_A1.RESET, Pololu_A1.SLEEP
  N7: Pololu_A1.STEP, Part2.D3_PWM
  N8: Pololu_A1.DIR, Part2.D2_PWM
  5V: Pololu_A1.VDD
  12V: Pololu_A1.VMOT, Part2.VIN, C1.+
  N9: Part2.A0, R1.P$2
  N10: Part2.A1, R2.P$2
  N11: Part2.A2, R3.P$2
  N12: Part2.A3, R4.P$2
  N13: Part2.D5_PWM, J2.Vout
  N14: R2.P$1, R6.Pin_1
  N15: R3.P$1, R7.Pin_1
  N16: R4.P$1, R8.Pin_1
  N17: R1.P$1, R5.Pin_1
